# Fritzing sketch SERVER (saved by Fritzing 0.9.3b)

parts:
  LCD1 = LCD screen  # not connected
  LED1 = LED - 3mm [color="Red (633nm)" package="3 mm [THT]"]
  LED2 = LED - 3mm [color="Red (633nm)" package="3 mm [THT]"]
  LED3 = LED - 3mm [color="Red (633nm)" package="3 mm [THT]"]
  LED4 = LED - 3mm [color="Red (633nm)" package="3 mm [THT]"]
  LED5 = LED - 3mm [color="Red (633nm)" package="3 mm [THT]"]
  LED6 = LED - 3mm [color="Red (633nm)" package="3 mm [THT]"]
  S4 = Momentary Switch [package=ksa_sealed_tac_switch]  # not connected
  J1 = Piezo Speaker  # not connected
  VCC2 = Battery block 9V  # not connected

nets:
  N1: LED1.anode, LED6.anode
  N2: LED2.anode, LED3.anode
  N3: LED4.anode, LED5.anode
