# Fritzing sketch CLIENT (saved by Fritzing 0.9.4)

parts:
  U1 = NodeMCU V3.0
  S4 = Round Pushbutton
  LED4 = LED - 5mm [color="Red (633nm)" package="5 mm [THT]"]
  BAT1 = BC9VPC [package=bc9vpc]
  J1 = Piezo Speaker

nets:
  N1: U1.D0, J1.pin2
  N2: U1.D4, S4.leg0
  N3: U1.GND#6, U1.GND#16, U1.GND#33, S4.leg1, LED4.anode, BAT1.V-
  N4: U1.D5, LED4.cathode
  N5: U1.Vin, BAT1.V+
  N6: U1.GND#41, J1.pin1

custom parts:
  NodeMCU V3.0: ESP8266 based NodeMCU
